# Fritzing sketch BlinkLCD-Sketch (saved by Fritzing 0.8.7b)
circuit board: 8.46667cm x 5.64444cm
breadboards: 1

parts:
  U1 = NodeMCU V1.0
  OLED_I2C1 = OLED 128x64 I2C Monochrome Display
  DS1 = DS18B20 1-Wire Temperature Sensor Probe Cable
  R1 = Resistor [tolerance=±20% resistance=4.7k package=THT]

nets:
  N1: U1.D1, OLED_I2C1.SCK
  N2: U1.D2, OLED_I2C1.SDA
  N3: U1.D4, DS1.DQ, R1.Pin_0
  VDD: U1.3V3, OLED_I2C1.VDD, DS1.VDD, R1.Pin_1
  GND: U1.GND, OLED_I2C1.GND, DS1.GND

custom parts:
  NodeMCU V1.0: ESP8266 based NodeMCU
